// Logisim project lab8A.circ as structural Verilog: 1 circuit, main circuit main
module main (
  input  B,
  input  C_in,
  input  A,
  output S,
  output C_out
);

  wire and_1_p3, and_2_out, and_3_out, and_4_out, and_5_out, and_6_out, and_7_out, not_1_p2, not_2_p2,
       not_3_p2, not_4_out, not_5_p2, not_6_p2;

  // NOT_Gate not_1: pin names not known; wires that end beside it: A, not_1_p2
  // NOT_Gate not_2: pin names not known; wires that end beside it: A, not_2_p2
  // NOT_Gate not_3: pin names not known; wires that end beside it: B, not_3_p2
  // NOT_Gate not_4 has open pins: in=open, out=not_4_out
  // NOT_Gate not_5: pin names not known; wires that end beside it: C_in, not_5_p2
  // NOT_Gate not_6: pin names not known; wires that end beside it: C_in, not_6_p2
  // AND_Gate and_1: pin names not known; wires that end beside it: A, C_in, and_1_p3
  and and_2 (and_2_out, C_in, B);
  and and_3 (and_3_out, B, A);
  and and_4 (and_4_out, not_1_p2, not_3_p2, C_in);
  and and_5 (and_5_out, not_6_p2, not_4_out, A);
  and and_6 (and_6_out, C_in, A, B);
  or or_1 (C_out, and_3_out, and_1_p3, and_2_out);
  and and_7 (and_7_out, B, not_2_p2, not_5_p2);
  or or_2 (S, and_7_out, and_4_out, and_6_out, and_5_out);

  // Notes on the sheet:
  //   These are the inputs
  //   of your circuit.
  //   Do not modify this!
  //   Put your name and id here: Yishui Sun - lab8 A
  //   This circuit is wrong :D
  //   Implement here your adder!
  //   These are the outputs
  //   of your circuit.
  //   Do not modify this!
endmodule
